// Logisim project Binary to gray code.circ as structural Verilog: 1 circuit, main circuit main
module main (
  input  B3,
  input  B2,
  input  B1,
  input  B0,
  output G0,
  output G2,
  output G1,
  output G0_2
);

  xor xor_1 (G0, B3, B2);
  xor xor_2 (G2, B2, B1);
  xor xor_3 (G1, B1, B0);

  assign G0_2 = B0;
endmodule
